# Fritzing sketch Melon_Green_v1.2.0_LEG12 (saved by Fritzing 0.9.3b)
circuit board: 15cm x 15cm
perfboards: 1

parts:
  U1_[AVR] = atmega328 [package=dip]
  J1 = female pin header, 3 pins [form="♀ (female)" part_number="Serial Port"]
  J2 = female pin header, 3 pins [form="♀ (female)" part_number="DHT Sensor"]
  J3 = female pin header, 3 pins [form="♀ (female)" part_number="Soil Moisture"]
  J4 = female pin header, 3 pins [form="♀ (female)" part_number="Food Level"]
  J5 = female pin header, 3 pins [form="♀ (female)" part_number="Rain Detector"]
  J6 = female pin header, 3 pins [form="♀ (female)" part_number="Light Sensor / LDR"]
  R1 = TRIMPOT [part_number=1K-10K package=trim_pot_pth]
  Sm1 = Pushbutton [part_number=Reset package="[THT]"]
  R2 = Resistor [tolerance=±5% resistance=10k part_number="DHT Pull-up" package=THT]
  XTAL = Crystal [frequency="16 Mhz" package=THT]
  C1 = Capacitor [part_number=22pF package=cap-pth-small2]
  C2 = Capacitor [part_number=22pF package=cap-pth-small2]
  R3 = Resistor [tolerance=±5% resistance=220 package=THT]
  R4 = Resistor [tolerance=±5% resistance=10k package=THT]
  LED1 = LED - 3mm [color="Yellow (595nm)" part_number=SVCC package="3 mm [THT]"]
  IC1 = Voltage Regulator [package=to-220-alt]
  C3 = Capacitor Polarized [part_number=10uF package=cpol-radial-10uf-25v]
  C4 = Capacitor Polarized [part_number=10uF package=cpol-radial-10uf-25v]
  R5 = Resistor [tolerance=±5% resistance=220 package=THT]
  LED2 = LED - 3mm [color="Red (633nm)" part_number=Power package="3 mm [THT]"]
  Sw1 = SPST Switch [part_number=Power package=switch-spdt_kit]
  J0 = male pin header, 2 pins [form="♂ (male)" part_number=~7-12vDC]
  R6 = Resistor [tolerance=±5% resistance=220 package=THT]
  LED3 = LED - 3mm [color="Green (555nm)" part_number="Debug Mode" package="3 mm [THT]"]  # not connected
  J7 = male pin header, 2 pins [form="♂ (male)" part_number="Debug Jumper"]
  J8 = female pin header, 4 pins [form="♀ (female)" part_number=RTC]
  OPT_01 = TLP621 [part_number=PC/EL817 package=THT]
  LED4 = LED - 3mm [color="Green (570nm)" part_number=IRIG package="3 mm [THT]"]
  OPT_2 = TLP621 [part_number=PC/EL817 package=THT]
  LED5 = LED - 3mm [color="Green (570nm)" part_number=GRLT package="3 mm [THT]"]
  OPT_3 = TLP621 [part_number=PC/EL817 package=THT]
  LED6 = LED - 3mm [color="Green (570nm)" part_number=FANC package="3 mm [THT]"]
  OPT_4 = TLP621 [part_number=PC/EL817 package=THT]
  LED7 = LED - 3mm [color="Green (570nm)" part_number=HEAT package="3 mm [THT]"]
  OPT_5 = TLP621 [part_number=PC/EL817 package=THT]
  LED8 = LED - 3mm [color="Green (570nm)" part_number=FOGR package="3 mm [THT]"]
  OPT_6 = TLP621 [part_number=PC/EL817 package=THT]
  LED9 = LED - 3mm [color="Green (570nm)" part_number=FRTL package="3 mm [THT]"]
  OPT_7 = TLP621 [part_number=PC/EL817 package=THT]
  LED10 = LED - 3mm [color="Green (570nm)" part_number=DLTR package="3 mm [THT]"]
  J9 = female pin header, 6 pins [form="♀ (female)" part_number="[USBasp] programmer"]
  JT_1 = screw terminal, 3 pins [part_number=Irrigation]
  JT_2 = screw terminal, 3 pins [part_number="Grow Light"]
  JT_3 = screw terminal, 3 pins [part_number="Fan / Cooler"]
  JT_4 = screw terminal, 3 pins [part_number=Heater]
  JT_5 = screw terminal, 3 pins [part_number=Humidifier]
  JT_6 = screw terminal, 3 pins [part_number=Fertilizer]
  JT_7 = screw terminal, 3 pins [part_number=Diluter]
  Q1 = TRANSISTOR_NPN [part_number=2N2222 package=to-92-ammo]
  R7 = Resistor [tolerance=±5% resistance=220 package=THT]
  R8 = Resistor [tolerance=±5% resistance=220 package=THT]
  R9 = Resistor [tolerance=±5% resistance=220 package=THT]
  R10 = Resistor [tolerance=±5% resistance=220 package=THT]
  R11 = Resistor [tolerance=±5% resistance=220 package=THT]
  R12 = Resistor [tolerance=±5% resistance=220 package=THT]
  R13 = Resistor [tolerance=±5% resistance=220 package=THT]
  R14 = Resistor [tolerance=±5% resistance=10k part_number="Rain Pull-Down" package=THT]
  J10 = male pin header, 3 pins [form="♂ (male)" part_number="RLY [Int/Ext] GND"]
  J12 = female pin header, 2 pins [form="♀ (female)" part_number="Ext RLY Power"]
  J11 = male pin header, 3 pins [form="♂ (male)" part_number="RLY [Int/Ext] Vcc"]
  J13 = male pin header, 2 pins [form="♂ (male)" part_number="~9v Rechargeable Battery"]
  D1 = Rectifier Diode [part_number=1N4007 breakdown_voltage=3.6V package="300 mil [THT]"]
  D2 = Rectifier Diode [part_number=1N4007 breakdown_voltage=3.6V package="300 mil [THT]"]
  R15 = Resistor [tolerance=±5% resistance=10k package=THT]
  RLY_1 = OMRON PCB Power Relay – G5LE [part_number="G5LE-1\n" package=THT]
  RLY_2 = OMRON PCB Power Relay – G5LE [part_number="G5LE-1\n" package=THT]
  RLY_3 = OMRON PCB Power Relay – G5LE [part_number="G5LE-1\n" package=THT]
  RLY_4 = OMRON PCB Power Relay – G5LE [part_number="G5LE-1\n" package=THT]
  RLY_5 = OMRON PCB Power Relay – G5LE [part_number="G5LE-1\n" package=THT]
  RLY_6 = OMRON PCB Power Relay – G5LE [part_number="G5LE-1\n" package=THT]
  RLY_7 = OMRON PCB Power Relay – G5LE [part_number="G5LE-1\n" package=THT]

nets (from the pcb view):
  N1: U1_[AVR].RESET, Sm1.Pin_1, Sm1.Pin_2, R4.Pin_1, J9.pin3
  N2: U1_[AVR].D0_(RX), J1.pin2
  N3: U1_[AVR].D1_(TX), J1.pin1
  N4: U1_[AVR].D2, Q1.B
  N5: U1_[AVR].D3_(PWM), J2.pin3, R2.Pin_0
  N6: U1_[AVR].D4, J5.pin3, R14.Pin_1
  N7: U1_[AVR].VCC, U1_[AVR].AVCC, R4.Pin_0, IC1.OUT, C4.+, LED2.anode, J7.pin2, J8.pin3, J9.pin1, Q1.C
  GND: U1_[AVR].GND, J1.pin3, J2.pin2, J3.pin2, J4.pin2, J5.pin2, J6.pin2, R1.CCW, Sm1.Pin_3, Sm1.Pin_4, C1.1, C2.1, R3.Pin_1, IC1.GND, C3.-, C4.-, R5.Pin_0, J0.pin1, J8.pin4, R7.Pin_1, R8.Pin_0, R9.Pin_0, R10.Pin_0, R11.Pin_0, R12.Pin_0, R13.Pin_0, R14.Pin_0, J10.pin1, J13.pin1
  N8: U1_[AVR].XLAT1, XTAL.pin_0, C1.2
  N9: U1_[AVR].XLAT2, XTAL.pin_1, C2.2
  N10: U1_[AVR].D5_(PWM), OPT_01.Pin_1
  N11: U1_[AVR].D6_(PWM), OPT_2.Pin_1
  N12: U1_[AVR].D7, OPT_3.Pin_1
  N13: U1_[AVR].D8, OPT_4.Pin_1
  N14: U1_[AVR].D9_(PWM), OPT_5.Pin_1
  N15: U1_[AVR].D11_(PWM), OPT_6.Pin_1, J9.pin4
  N16: U1_[AVR].D12, OPT_7.Pin_1, J9.pin5
  N17: U1_[AVR].D13, J9.pin6
  N18: U1_[AVR].A0, J7.pin1
  N19: U1_[AVR].A1, J3.pin3
  N20: U1_[AVR].A2, R1.CW
  N21: U1_[AVR].A3, J4.pin3
  N22: U1_[AVR].A4, J8.pin2
  N23: U1_[AVR].A5, J8.pin1
  N24: J2.pin1, J3.pin1, J4.pin1, J5.pin1, J6.pin1, R2.Pin_1, LED1.anode, Q1.E
  N25: J6.pin3, R1.WIPER
  N26: R3.Pin_0, LED1.cathode
  N27: IC1.IN, C3.+, Sw1.O
  N28: R5.Pin_1, LED2.cathode
  N29: Sw1.P, D1.cathode, D2.cathode
  N30: J0.pin2, J11.pin1, D1.anode, R15.Pin_0
  N31: R6.Pin_1, J9.pin2
  N32: OPT_01.Pin_2, LED4.anode
  N33: OPT_01.Pin_4, OPT_2.Pin_4, OPT_3.Pin_4, OPT_4.Pin_4, OPT_5.Pin_4, OPT_6.Pin_4, OPT_7.Pin_4, J11.pin2
  N34: OPT_01.Pin_3, RLY_1.COIL1
  N35: LED4.cathode, R7.Pin_0
  N36: OPT_2.Pin_2, LED5.anode
  N37: OPT_2.Pin_3, RLY_2.COIL1
  N38: LED5.cathode, R8.Pin_1
  N39: OPT_3.Pin_2, LED6.anode
  N40: OPT_3.Pin_3, RLY_3.COIL1
  N41: LED6.cathode, R9.Pin_1
  N42: OPT_4.Pin_2, LED7.anode
  N43: OPT_4.Pin_3, RLY_4.COIL1
  N44: LED7.cathode, R10.Pin_1
  N45: OPT_5.Pin_2, LED8.anode
  N46: OPT_5.Pin_3, RLY_5.COIL1
  N47: LED8.cathode, R11.Pin_1
  N48: OPT_6.Pin_2, LED9.anode
  N49: OPT_6.Pin_3, RLY_6.COIL1
  N50: LED9.cathode, R12.Pin_1
  N51: OPT_7.Pin_2, LED10.anode
  N52: OPT_7.Pin_3, RLY_7.COIL1
  N53: LED10.cathode, R13.Pin_1
  N54: JT_1.pin1, RLY_1.A
  N55: JT_1.pin2, RLY_1.C
  N56: JT_1.pin3, RLY_1.B
  N57: JT_2.pin1, RLY_2.A
  N58: JT_2.pin2, RLY_2.C
  N59: JT_2.pin3, RLY_2.B
  N60: JT_3.pin1, RLY_3.A
  N61: JT_3.pin2, RLY_3.C
  N62: JT_3.pin3, RLY_3.B
  N63: JT_4.pin1, RLY_4.A
  N64: JT_4.pin2, RLY_4.C
  N65: JT_4.pin3, RLY_4.B
  N66: JT_5.pin1, RLY_5.A
  N67: JT_5.pin2, RLY_5.C
  N68: JT_5.pin3, RLY_5.B
  N69: JT_6.pin1, RLY_6.A
  N70: JT_6.pin2, RLY_6.C
  N71: JT_6.pin3, RLY_6.B
  N72: JT_7.pin1, RLY_7.A
  N73: JT_7.pin2, RLY_7.C
  N74: JT_7.pin3, RLY_7.B
  N75: J10.pin2, RLY_1.COIL2, RLY_2.COIL2, RLY_3.COIL2, RLY_4.COIL2, RLY_5.COIL2, RLY_6.COIL2, RLY_7.COIL2
  N76: J10.pin3, J12.pin1
  N77: J12.pin2, J11.pin3
  N78: J13.pin2, D2.anode, R15.Pin_1

notes:
  Tx Rx Gnd
  [Note] Sensors Terminals pin mapping (left to right) : VCC GND Data
  VGD
  +
  -
  LDR Pull-Down
  SDA
  SCL
  VCC
  GND
  Melon Green
  Morteza H. Golkar
  2017
  RTS
  SCK
  MISO
  MOSI
  )
  v1.2.0
  Melon Green v1.2.0
